// Logisim project congress.circ as structural Verilog: 3 circuits, main circuit main
module main (
  input  in_1
);

  wire alu_1_out_5, and_1_out, and_2_out, and_3_out, and_4_out, and_5_out, and_6_out, and_7_out, and_8_out,
       and_9_out, clock_1_out, comparator_1_eq, nand_1_out, nor_1_out, nor_2_out, not_1_out, not_2_out,
       not_3_out, not_4_out, not_5_out, not_6_out, not_7_out, not_8_out, not_9_out, not_10_out, not_11_out,
       or_1_out, or_2_out, undriven;
  wire [7:0] A_q, alu_1_out_4, B_q, data_dout, multiplexer_1_out, multiplexer_2_out, multiplexer_3_out;
  wire [11:0] pc_1_out_9;
  wire [15:0] inststructions_dout;

  Clock clock_1 (.out(clock_1_out));
  RAM #(.addrWidth(12), .dataWidth(16), .enables("line")) inststructions (
    .addr(pc_1_out_9), .clk(clock_1_out), .dout(inststructions_dout));  // open: we, din
  PC pc_1 (
    .in_1(inststructions_dout[15:4]), .jmp(and_4_out), .jz(and_1_out), .je(and_2_out), .jc(and_5_out),
    .en(in_1), .halt(and_3_out), .clk(clock_1_out), .out_9(pc_1_out_9));
  nor nor_1 (nor_1_out, A_q[0], A_q[1], A_q[2], A_q[3], A_q[4], A_q[5], A_q[6], A_q[7]);
  and and_1 (and_1_out, nor_1_out, inststructions_dout[0], inststructions_dout[1], not_1_out, inststructions_dout[3]);
  not not_1 (not_1_out, inststructions_dout[2]);
  and and_2 (and_2_out, comparator_1_eq, inststructions_dout[0], not_2_out, inststructions_dout[2], inststructions_dout[3]);
  not not_2 (not_2_out, inststructions_dout[1]);
  not not_3 (not_3_out, inststructions_dout[1]);
  and and_3 (and_3_out, inststructions_dout[0], not_3_out, not_4_out, inststructions_dout[3]);
  not not_4 (not_4_out, inststructions_dout[2]);
  not not_5 (not_5_out, inststructions_dout[0]);
  and and_4 (and_4_out, not_5_out, inststructions_dout[1], not_6_out, inststructions_dout[3]);
  not not_6 (not_6_out, inststructions_dout[2]);
  not not_7 (not_7_out, inststructions_dout[0]);
  and and_5 (and_5_out, alu_1_out_5, not_7_out, not_8_out, inststructions_dout[2], inststructions_dout[3]);
  not not_8 (not_8_out, inststructions_dout[1]);
  Comparator #(.mode("unsigned")) comparator_1 (.a(A_q), .b(B_q), .eq(comparator_1_eq));  // open: gt, lt
  or or_1 (or_1_out, inststructions_dout[0], inststructions_dout[1], inststructions_dout[2]);
  not not_9 (not_9_out, inststructions_dout[3]);
  not not_10 (not_10_out, inststructions_dout[4]);
  not not_11 (not_11_out, inststructions_dout[3]);
  and and_6 (and_6_out, nand_1_out, or_1_out, not_9_out);
  nand nand_1 (nand_1_out, inststructions_dout[0], inststructions_dout[1], inststructions_dout[2]);
  and and_7 (and_7_out, inststructions_dout[0], inststructions_dout[1], not_10_out, inststructions_dout[2], not_11_out);
  and and_8 (and_8_out, inststructions_dout[0], inststructions_dout[1], inststructions_dout[4], inststructions_dout[2], not_11_out);
  nor nor_2 (nor_2_out, inststructions_dout[2], inststructions_dout[1], inststructions_dout[0]);
  ALU alu_1 (.in_1(A_q), .in_2(B_q), .in_3(inststructions_dout[2:0]), .out_4(alu_1_out_4), .out_5(alu_1_out_5));
  and and_9 (and_9_out, nor_2_out, inststructions_dout[3]);
  Multiplexer #(.width(8)) multiplexer_1 (.in0(alu_1_out_4), .in1(data_dout), .out(multiplexer_1_out), .sel(and_7_out));
  or or_2 (or_2_out, and_7_out, and_6_out);
  Multiplexer #(.width(8)) multiplexer_2 (.in0(B_q), .in1(data_dout), .out(multiplexer_2_out), .sel(and_8_out));
  Register A (.D(multiplexer_1_out), .en(or_2_out), .clk(clock_1_out), .Q(A_q), .clr(undriven));
  Register B (.D(multiplexer_2_out), .en(and_8_out), .clk(clock_1_out), .Q(B_q));  // open: clr
  RAM #(.addrWidth(10), .enables("line")) data (
    .addr(inststructions_dout[14:5]), .we(and_9_out), .clk(clock_1_out), .din(multiplexer_3_out),
    .dout(data_dout));
  Multiplexer #(.width(8)) multiplexer_3 (.in0(A_q), .in1(B_q), .out(multiplexer_3_out), .sel(inststructions_dout[4]));
endmodule

module ALU (
  input  [7:0] in_1,
  input  [7:0] in_2,
  input  [2:0] in_3,
  output [7:0] out_4,
  output out_5
);

  wire [7:0] adder_1_out, and_1_out, not_1_out, or_1_out, subtractor_1_out, xor_1_out;

  assign and_1_out = in_1 & in_2;  // AND_Gate and_1, 8 bits wide
  assign or_1_out = in_1 | in_2;  // OR_Gate or_1, 8 bits wide
  assign xor_1_out = in_1 ^ in_2;  // XOR_Gate xor_1, 8 bits wide
  assign not_1_out = ~in_1;  // NOT_Gate not_1, 8 bits wide
  Adder adder_1 (.a(in_1), .b(in_2), .out(adder_1_out), .cout(out_5));  // open: cin
  Subtractor subtractor_1 (.a(in_1), .b(in_2), .out(subtractor_1_out));  // open: bin, bout
  Multiplexer #(.select(3), .width(8)) multiplexer_1 (
    .in0(in_1), .in1(and_1_out), .in2(or_1_out), .in3(xor_1_out), .in4(not_1_out), .in5(adder_1_out),
    .in6(subtractor_1_out), .out(out_4), .sel(in_3));  // open: in7
endmodule

module PC (
  input  [11:0] in_1,
  input  jmp,
  input  jz,
  input  je,
  input  jc,
  input  en,
  input  halt,
  input  clk,
  output [11:0] out_9
);

  wire nor_1_out, not_1_out, or_1_out, s_r_ff_1_q;
  wire [11:0] adder_1_out, controlled_buffer_1_out;

  Adder #(.width(12)) adder_1 (.a(out_9), .b(12'h1), .out(adder_1_out));  // open: cin, cout
  assign controlled_buffer_1_out = nor_1_out ? adder_1_out : 12'bz;  // Controlled_Buffer controlled_buffer_1
  assign controlled_buffer_1_out = jz ? in_1 : 12'bz;  // Controlled_Buffer controlled_buffer_2
  assign controlled_buffer_1_out = je ? in_1 : 12'bz;  // Controlled_Buffer controlled_buffer_3
  nor nor_1 (nor_1_out, jz, jmp, je, jc);
  assign controlled_buffer_1_out = jmp ? in_1 : 12'bz;  // Controlled_Buffer controlled_buffer_4
  assign controlled_buffer_1_out = jc ? in_1 : 12'bz;  // Controlled_Buffer controlled_buffer_5
  Register #(.width(12)) register_1 (.D(controlled_buffer_1_out), .en(en), .clk(clk), .Q(out_9), .clr(or_1_out));
  or or_1 (or_1_out, not_1_out, s_r_ff_1_q);
  S_R_Flip_Flop s_r_ff_1 (.S(halt), .R(not_1_out), .clk(clk), .Q(s_r_ff_1_q));  // open: reset, Qn, preset
  not not_1 (not_1_out, en);
endmodule
